# Fritzing sketch uno (saved by Fritzing 0.9.3b)
breadboards: 1

parts:
  부품1 = Arduino Ethernet Shield (Rev3)
  S1 = Pushbutton [package="[THT]"]
  S2 = Pushbutton [package="[THT]"]
  R1 = Rotary Potentiometer (Small) [maximum_resistance=100kΩ package=THT]
  R2 = Rotary Potentiometer (Small) [maximum_resistance=100kΩ package=THT]

nets:
  N1: 부품1.A0, R2.wiper
  N2: 부품1.A1, R1.wiper
  N3: 부품1.PWM_D3, S2.Pin_4
  N4: 부품1.PWM_D6, S1.Pin_4
  N5: 부품1.5V, R1.leg2, R2.leg1
  N6: 부품1.GND, S1.Pin_1, S2.Pin_1, S2.Pin_2, R1.leg1, R2.leg2
